// Logisim project Final__.circ as structural Verilog: 11 circuits, main circuit CPU
module BC (
  input  Enable,
  input  Input,
  input  Clock,
  input  R___W,
  output Output
);

  wire and_1_out, and_2_out, not_1_out, not_2_out, s_r_ff_1_q;

  not not_1 (not_1_out, Input);
  not not_2 (not_2_out, R___W);
  and and_1 (and_1_out, Enable, not_1_out, not_2_out);
  and and_2 (and_2_out, Input, Enable, not_2_out);
  S_R_Flip_Flop s_r_ff_1 (.S(and_2_out), .clk(Clock), .R(and_1_out), .Q(s_r_ff_1_q));  // open: Qn, preset, reset, en
  and and_3 (Output, s_r_ff_1_q, Enable, R___W);
endmodule

module _4x4 (
  input  I0,
  input  I1,
  input  I2,
  input  I3,
  input  E,
  input  [1:0] Addr,
  input  R_W,
  output O0,
  output O1,
  output O2,
  output O3
);

  wire bc_1_output, bc_2_output, bc_3_output, bc_4_output, bc_5_output, bc_6_output, bc_7_output,
       bc_8_output, bc_9_output, bc_10_output, bc_11_output, bc_12_output, bc_13_output, bc_14_output,
       bc_15_output, bc_16_output, clock_1_out, decoder_1_out0, decoder_1_out1, decoder_1_out2,
       decoder_1_out3, or_1_out, or_2_out, or_3_out, or_4_out;

  Decoder #(.select(2)) decoder_1 (
    .out0(decoder_1_out0), .out1(decoder_1_out1), .out2(decoder_1_out2), .out3(decoder_1_out3), .sel(Addr),
    .en(E));
  Clock clock_1 (.out(clock_1_out));
  BC bc_1 (.Input(I0), .Clock(clock_1_out), .Enable(decoder_1_out0), .R___W(R_W), .Output(bc_1_output));
  BC bc_2 (.Input(I0), .Clock(clock_1_out), .Enable(decoder_1_out1), .R___W(R_W), .Output(bc_2_output));
  BC bc_3 (.Input(I0), .Clock(clock_1_out), .Enable(decoder_1_out2), .R___W(R_W), .Output(bc_3_output));
  BC bc_4 (.Input(I0), .Clock(clock_1_out), .Enable(decoder_1_out3), .R___W(R_W), .Output(bc_4_output));
  or or_1 (or_1_out, bc_3_output, bc_2_output, bc_1_output, bc_4_output);
  BC bc_5 (.Input(I1), .Clock(clock_1_out), .Enable(decoder_1_out0), .R___W(R_W), .Output(bc_5_output));
  BC bc_6 (.Input(I1), .Clock(clock_1_out), .Enable(decoder_1_out1), .R___W(R_W), .Output(bc_6_output));
  BC bc_7 (.Input(I1), .Clock(clock_1_out), .Enable(decoder_1_out2), .R___W(R_W), .Output(bc_7_output));
  BC bc_8 (.Input(I1), .Clock(clock_1_out), .Enable(decoder_1_out3), .R___W(R_W), .Output(bc_8_output));
  or or_2 (or_2_out, bc_7_output, bc_6_output, bc_5_output, bc_8_output);
  and and_1 (O0, or_1_out, E);
  BC bc_9 (.Input(I2), .Clock(clock_1_out), .Enable(decoder_1_out0), .R___W(R_W), .Output(bc_9_output));
  BC bc_10 (.Input(I2), .Clock(clock_1_out), .Enable(decoder_1_out1), .R___W(R_W), .Output(bc_10_output));
  BC bc_11 (.Input(I2), .Clock(clock_1_out), .Enable(decoder_1_out2), .R___W(R_W), .Output(bc_11_output));
  BC bc_12 (.Input(I2), .Clock(clock_1_out), .Enable(decoder_1_out3), .R___W(R_W), .Output(bc_12_output));
  and and_2 (O1, or_2_out, E);
  BC bc_13 (.Input(I3), .Clock(clock_1_out), .Enable(decoder_1_out0), .R___W(R_W), .Output(bc_13_output));
  BC bc_14 (.Input(I3), .Clock(clock_1_out), .Enable(decoder_1_out1), .R___W(R_W), .Output(bc_14_output));
  BC bc_15 (.Input(I3), .Clock(clock_1_out), .Enable(decoder_1_out2), .R___W(R_W), .Output(bc_15_output));
  BC bc_16 (.Input(I3), .Clock(clock_1_out), .Enable(decoder_1_out3), .R___W(R_W), .Output(bc_16_output));
  or or_3 (or_3_out, bc_11_output, bc_10_output, bc_9_output, bc_12_output);
  and and_3 (O2, or_3_out, E);
  or or_4 (or_4_out, bc_16_output, bc_15_output, bc_14_output, bc_13_output);
  and and_4 (O3, or_4_out, E);
endmodule

module _32x4 (
  input  I0,
  input  I1,
  input  I2,
  input  I3,
  input  E,
  input  [4:0] Addr,
  input  R_W,
  output O0,
  output O1,
  output O2,
  output O3
);

  wire decoder_1_out0, decoder_1_out1, decoder_1_out2, decoder_1_out3, decoder_1_out4, decoder_1_out5,
       decoder_1_out6, decoder_1_out7, n4x4_1_o0, n4x4_1_o1, n4x4_1_o2, n4x4_1_o3, n4x4_2_o0, n4x4_2_o1,
       n4x4_2_o2, n4x4_2_o3, n4x4_3_o0, n4x4_3_o1, n4x4_3_o2, n4x4_3_o3, n4x4_4_o0, n4x4_4_o1, n4x4_4_o2,
       n4x4_4_o3, n4x4_5_o0, n4x4_5_o1, n4x4_5_o2, n4x4_5_o3, n4x4_6_o0, n4x4_6_o1, n4x4_6_o2, n4x4_6_o3,
       n4x4_7_o0, n4x4_7_o1, n4x4_7_o2, n4x4_7_o3, n4x4_8_o0, n4x4_8_o1, n4x4_8_o2, n4x4_8_o3, or_1_out,
       or_2_out, or_3_out, or_4_out;

  Decoder #(.select(3)) decoder_1 (
    .out0(decoder_1_out0), .out1(decoder_1_out1), .out2(decoder_1_out2), .out3(decoder_1_out3),
    .out4(decoder_1_out4), .out5(decoder_1_out5), .out6(decoder_1_out6), .out7(decoder_1_out7),
    .sel(Addr[4:2]), .en(E));
  _4x4 u_4x4_1 (
    .E(decoder_1_out0), .Addr(Addr[1:0]), .R_W(R_W), .I0(I0), .I1(I1), .I2(I2), .I3(I3), .O0(n4x4_1_o0),
    .O1(n4x4_1_o1), .O2(n4x4_1_o2), .O3(n4x4_1_o3));
  _4x4 u_4x4_2 (
    .E(decoder_1_out1), .Addr(Addr[1:0]), .R_W(R_W), .I0(I0), .I1(I1), .I2(I2), .I3(I3), .O0(n4x4_2_o0),
    .O1(n4x4_2_o1), .O2(n4x4_2_o2), .O3(n4x4_2_o3));
  _4x4 u_4x4_3 (
    .E(decoder_1_out2), .Addr(Addr[1:0]), .R_W(R_W), .I0(I0), .I1(I1), .I2(I2), .I3(I3), .O0(n4x4_3_o0),
    .O1(n4x4_3_o1), .O2(n4x4_3_o2), .O3(n4x4_3_o3));
  _4x4 u_4x4_4 (
    .E(decoder_1_out3), .Addr(Addr[1:0]), .R_W(R_W), .I0(I0), .I1(I1), .I2(I2), .I3(I3), .O0(n4x4_4_o0),
    .O1(n4x4_4_o1), .O2(n4x4_4_o2), .O3(n4x4_4_o3));
  _4x4 u_4x4_5 (
    .E(decoder_1_out4), .Addr(Addr[1:0]), .R_W(R_W), .I0(I0), .I1(I1), .I2(I2), .I3(I3), .O0(n4x4_5_o0),
    .O1(n4x4_5_o1), .O2(n4x4_5_o2), .O3(n4x4_5_o3));
  _4x4 u_4x4_6 (
    .E(decoder_1_out5), .Addr(Addr[1:0]), .R_W(R_W), .I0(I0), .I1(I1), .I2(I2), .I3(I3), .O0(n4x4_6_o0),
    .O1(n4x4_6_o1), .O2(n4x4_6_o2), .O3(n4x4_6_o3));
  _4x4 u_4x4_7 (
    .E(decoder_1_out6), .Addr(Addr[1:0]), .R_W(R_W), .I0(I0), .I1(I1), .I2(I2), .I3(I3), .O0(n4x4_7_o0),
    .O1(n4x4_7_o1), .O2(n4x4_7_o2), .O3(n4x4_7_o3));
  _4x4 u_4x4_8 (
    .E(decoder_1_out7), .Addr(Addr[1:0]), .R_W(R_W), .I0(I0), .I1(I1), .I2(I2), .I3(I3), .O0(n4x4_8_o0),
    .O1(n4x4_8_o1), .O2(n4x4_8_o2), .O3(n4x4_8_o3));
  or or_1 (or_1_out, n4x4_1_o0, n4x4_2_o0, n4x4_3_o0, n4x4_4_o0, n4x4_5_o0, n4x4_6_o0, n4x4_7_o0, n4x4_8_o0);
  or or_2 (or_2_out, n4x4_1_o1, n4x4_2_o1, n4x4_3_o1, n4x4_4_o1, n4x4_5_o1, n4x4_6_o1, n4x4_7_o1, n4x4_8_o1);
  or or_3 (or_3_out, n4x4_1_o2, n4x4_2_o2, n4x4_3_o2, n4x4_4_o2, n4x4_5_o2, n4x4_6_o2, n4x4_7_o2, n4x4_8_o2);
  or or_4 (or_4_out, n4x4_1_o3, n4x4_2_o3, n4x4_3_o3, n4x4_4_o3, n4x4_5_o3, n4x4_6_o3, n4x4_7_o3, n4x4_8_o3);
  and and_1 (O0, or_1_out, E);
  and and_2 (O1, or_2_out, E);
  and and_3 (O2, or_3_out, E);
  and and_4 (O3, or_4_out, E);
endmodule

module TEMP (
  input  in_1,
  input  in_2,
  input  in_3,
  input  in_4,
  input  in_5,
  input  [7:0] in_6,
  input  in_7
);

  wire n256x4_1_o0, n256x4_1_o1, n256x4_1_o2, n256x4_1_o3;

  _256X4 u_256x4_1 (
    .E(in_5), .Addr(in_6), .R_W(in_7), .I0(in_1), .I1(in_2), .I2(in_3), .I3(in_4), .O0(n256x4_1_o0),
    .O1(n256x4_1_o1), .O2(n256x4_1_o2), .O3(n256x4_1_o3));
  LED led_1 (.in(n256x4_1_o0));
  LED led_2 (.in(n256x4_1_o2));
  LED led_3 (.in(n256x4_1_o3));
  LED led_4 (.in(n256x4_1_o1));
endmodule

// Memory
module _256X4 (
  input  I0,
  input  I1,
  input  I2,
  input  I3,
  input  E,
  input  [7:0] Addr,
  input  R_W,
  output O0,
  output O1,
  output O2,
  output O3
);

  wire decoder_1_out0, decoder_1_out1, decoder_1_out2, decoder_1_out3, decoder_1_out4, decoder_1_out5,
       decoder_1_out6, decoder_1_out7, n32x4_1_o0, n32x4_1_o1, n32x4_1_o2, n32x4_1_o3, n32x4_2_o0,
       n32x4_2_o1, n32x4_2_o2, n32x4_2_o3, n32x4_3_o0, n32x4_3_o1, n32x4_3_o2, n32x4_3_o3, n32x4_4_o0,
       n32x4_4_o1, n32x4_4_o2, n32x4_4_o3, n32x4_5_o0, n32x4_5_o1, n32x4_5_o2, n32x4_5_o3, n32x4_6_o0,
       n32x4_6_o1, n32x4_6_o2, n32x4_6_o3, n32x4_7_o0, n32x4_7_o1, n32x4_7_o2, n32x4_7_o3, n32x4_8_o0,
       n32x4_8_o1, n32x4_8_o2, n32x4_8_o3, or_1_out, or_2_out, or_3_out, or_4_out;

  Decoder #(.select(3)) decoder_1 (
    .out0(decoder_1_out0), .out1(decoder_1_out1), .out2(decoder_1_out2), .out3(decoder_1_out3),
    .out4(decoder_1_out4), .out5(decoder_1_out5), .out6(decoder_1_out6), .out7(decoder_1_out7),
    .sel(Addr[7:5]), .en(E));
  _32x4 u_32x4_1 (
    .E(decoder_1_out0), .Addr(Addr[4:0]), .R_W(R_W), .I0(I0), .I1(I1), .I2(I2), .I3(I3), .O0(n32x4_1_o0),
    .O1(n32x4_1_o1), .O2(n32x4_1_o2), .O3(n32x4_1_o3));
  _32x4 u_32x4_2 (
    .E(decoder_1_out1), .Addr(Addr[4:0]), .R_W(R_W), .I0(I0), .I1(I1), .I2(I2), .I3(I3), .O0(n32x4_2_o0),
    .O1(n32x4_2_o1), .O2(n32x4_2_o2), .O3(n32x4_2_o3));
  _32x4 u_32x4_3 (
    .E(decoder_1_out2), .Addr(Addr[4:0]), .R_W(R_W), .I0(I0), .I1(I1), .I2(I2), .I3(I3), .O0(n32x4_3_o0),
    .O1(n32x4_3_o1), .O2(n32x4_3_o2), .O3(n32x4_3_o3));
  _32x4 u_32x4_4 (
    .E(decoder_1_out3), .Addr(Addr[4:0]), .R_W(R_W), .I0(I0), .I1(I1), .I2(I2), .I3(I3), .O0(n32x4_4_o0),
    .O1(n32x4_4_o1), .O2(n32x4_4_o2), .O3(n32x4_4_o3));
  _32x4 u_32x4_5 (
    .E(decoder_1_out4), .Addr(Addr[4:0]), .R_W(R_W), .I0(I0), .I1(I1), .I2(I2), .I3(I3), .O0(n32x4_5_o0),
    .O1(n32x4_5_o1), .O2(n32x4_5_o2), .O3(n32x4_5_o3));
  _32x4 u_32x4_6 (
    .E(decoder_1_out5), .Addr(Addr[4:0]), .R_W(R_W), .I0(I0), .I1(I1), .I2(I2), .I3(I3), .O0(n32x4_6_o0),
    .O1(n32x4_6_o1), .O2(n32x4_6_o2), .O3(n32x4_6_o3));
  _32x4 u_32x4_7 (
    .E(decoder_1_out6), .Addr(Addr[4:0]), .R_W(R_W), .I0(I0), .I1(I1), .I2(I2), .I3(I3), .O0(n32x4_7_o0),
    .O1(n32x4_7_o1), .O2(n32x4_7_o2), .O3(n32x4_7_o3));
  _32x4 u_32x4_8 (
    .E(decoder_1_out7), .Addr(Addr[4:0]), .R_W(R_W), .I0(I0), .I1(I1), .I2(I2), .I3(I3), .O0(n32x4_8_o0),
    .O1(n32x4_8_o1), .O2(n32x4_8_o2), .O3(n32x4_8_o3));
  or or_1 (or_1_out, n32x4_1_o0, n32x4_2_o0, n32x4_3_o0, n32x4_4_o0, n32x4_5_o0, n32x4_6_o0, n32x4_7_o0, n32x4_8_o0);
  or or_2 (or_2_out, n32x4_1_o1, n32x4_2_o1, n32x4_3_o1, n32x4_4_o1, n32x4_5_o1, n32x4_6_o1, n32x4_7_o1, n32x4_8_o1);
  or or_3 (or_3_out, n32x4_1_o2, n32x4_2_o2, n32x4_3_o2, n32x4_4_o2, n32x4_5_o2, n32x4_6_o2, n32x4_7_o2, n32x4_8_o2);
  or or_4 (or_4_out, n32x4_1_o3, n32x4_2_o3, n32x4_3_o3, n32x4_4_o3, n32x4_5_o3, n32x4_6_o3, n32x4_7_o3, n32x4_8_o3);
  and and_1 (O0, or_1_out, E);
  and and_2 (O1, or_2_out, E);
  and and_3 (O2, or_3_out, E);
  and and_4 (O3, or_4_out, E);
endmodule

// IU
module InputUnit (
  input  [3:0] A,
  input  [3:0] B,
  input  Addr_Enable,
  input  DataSwitch,
  output [3:0] Data,
  output [7:0] Address
);

  wire [7:0] adder_1_out, AddressGen_out;

  Random AddressGen (.clk(Addr_Enable), .out(AddressGen_out));  // open: next, clr
  Adder adder_1 (.a(AddressGen_out), .b(8'h1), .out(adder_1_out));  // open: cin, cout
  Multiplexer #(.width(4), .enable("false")) multiplexer_1 (.in0(A), .in1(B), .out(Data), .sel(DataSwitch));
  Multiplexer #(.width(8), .enable("false")) multiplexer_2 (
    .in0(AddressGen_out), .in1(adder_1_out), .out(Address), .sel(DataSwitch));
endmodule

module ALU (
  input  [3:0] A,
  input  Enable,
  input  [3:0] B,
  input  [1:0] Select,
  output Overflow,
  output [3:0] Output,
  output [3:0] MulCarryOut
);

  wire adder_1_cout, subtractor_1_bout;
  wire [3:0] adder_1_out, multiplier_1_cout, multiplier_1_out, or_1_out, subtractor_1_out;

  Adder #(.width(4)) adder_1 (.a(A), .b(B), .out(adder_1_out), .cout(adder_1_cout));  // open: cin
  Subtractor #(.width(4)) subtractor_1 (.a(A), .b(B), .out(subtractor_1_out), .bout(subtractor_1_bout));  // open: bin
  assign or_1_out = A | B;  // OR_Gate or_1, 4 bits wide
  Multiplier #(.width(4)) multiplier_1 (.a(A), .b(B), .out(multiplier_1_out), .cout(multiplier_1_cout));  // open: cin
  Multiplexer #(.select(2)) multiplexer_1 (
    .in0(adder_1_cout), .in1(subtractor_1_bout), .out(Overflow), .sel(Select), .en(Enable));  // open: in2, in3
  Multiplexer #(.select(2), .width(4)) multiplexer_2 (
    .in0(adder_1_out), .in1(subtractor_1_out), .in2(or_1_out), .in3(multiplier_1_out), .out(Output),
    .sel(Select), .en(Enable));
  Demultiplexer #(.select(2), .width(4)) demultiplexer_1 (
    .out3(MulCarryOut), .in(multiplier_1_cout), .sel(Select), .en(Enable));  // open: out0, out1, out2
endmodule

module OutputUnit (
  input  [3:0] in_1,
  output a,
  output out_3,
  output out_4,
  output out_5,
  output out_6,
  output out_7,
  output out_8
);

  // _7_segment_display_driver 7_segment_display_driver_1: pin names not known; wires that end beside it: in_1[3], in_1[2], in_1[1], in_1[0], a, out_3, out_4, out_5, out_6, out_7, out_8
  _7_Segment_Display u_7_segment_display_1 (
    .g(out_8), .f(out_7), .a(a), .b(out_3), .e(out_6), .d(out_5), .c(out_4));  // open: dp
endmodule

// CPU
module Main (
  input  [3:0] A,
  input  [3:0] B,
  input  Enable,
  input  Load_B,
  input  [1:0] L___F,
  input  [1:0] OP_code,
  output Overflow,
  output [3:0] Output,
  output [3:0] MulCarryOut
);

  wire and_1_out, and_2_out, and_3_out, clk_out, not_1_out, not_2_out, not_3_out, Read_Write_out;
  wire [3:0] alu_1_output, Data_A_q, Data_B_q, demultiplexer_1_out1, demultiplexer_1_out2, inputunit_1_data,
       n256x4_1_o3;
  wire [7:0] inputunit_1_address, multiplexer_1_out, REG1_q, REG2_q;

  InputUnit inputunit_1 (
    .A(A), .B(B), .Addr_Enable(Enable), .DataSwitch(Load_B), .Data(inputunit_1_data),
    .Address(inputunit_1_address));
  not not_1 (not_1_out, Load_B);
  Clock clk (.out(clk_out));
  Register REG2 (.D(inputunit_1_address), .en(Load_B), .Q(REG2_q), .clk(clk_out));  // open: clr
  Register REG1 (.D(inputunit_1_address), .en(not_1_out), .Q(REG1_q), .clk(clk_out));  // open: clr
  Multiplexer #(.select(2), .width(8), .enable("false")) multiplexer_1 (
    .in0(inputunit_1_address), .in1(REG1_q), .in2(REG2_q), .out(multiplexer_1_out), .sel(L___F));  // open: in3
  xor Read_Write (Read_Write_out, L___F[0], L___F[1]);
  and and_1 (and_1_out, L___F[0], L___F[1]);
  not not_2 (not_2_out, L___F[0]);
  not not_3 (not_3_out, L___F[1]);
  _256X4 u_256x4_1 (
    .E(Enable), .Addr(multiplexer_1_out), .R_W(Read_Write_out), .I0(inputunit_1_data[3]),
    .I1(inputunit_1_data[2]), .I2(inputunit_1_data[1]), .I3(inputunit_1_data[0]), .O0(n256x4_1_o3[3]),
    .O1(n256x4_1_o3[2]), .O2(n256x4_1_o3[1]), .O3(n256x4_1_o3[0]));
  Demultiplexer #(.select(2), .width(4), .enable("false")) demultiplexer_1 (
    .out1(demultiplexer_1_out1), .out2(demultiplexer_1_out2), .in(n256x4_1_o3), .sel(L___F));  // open: out0, out3
  and and_2 (and_2_out, L___F[1], not_2_out);
  and and_3 (and_3_out, L___F[0], not_3_out);
  Register #(.width(4)) Data_A (.D(demultiplexer_1_out1), .en(and_3_out), .Q(Data_A_q), .clk(clk_out));  // open: clr
  Register #(.width(4)) Data_B (.D(demultiplexer_1_out2), .en(and_2_out), .Q(Data_B_q), .clk(clk_out));  // open: clr
  ALU alu_1 (
    .A(Data_A_q), .B(Data_B_q), .Select(OP_code), .Enable(and_1_out), .Overflow(Overflow),
    .Output(alu_1_output), .MulCarryOut(MulCarryOut));
  Multiplexer #(.select(2), .width(4), .enable("false")) multiplexer_2 (
    .in0(n256x4_1_o3), .in1(n256x4_1_o3), .in2(n256x4_1_o3), .in3(alu_1_output), .out(Output), .sel(L___F));
  Hex_Digit_Display hex_digit_display_1 (.value(Output));  // open: dp
endmodule

module CPU (
  input  [3:0] A,
  input  [3:0] B,
  input  Power,
  output [1:0] out_4,
  output [1:0] out_5
);

  wire L_F_Control_out, Load_out, main_1_overflow, OperationControl_out;
  wire [3:0] main_1_mulcarryout, main_1_output;

  Button Load (.out(Load_out));
  Button L_F_Control (.out(L_F_Control_out));
  ButtonController buttoncontroller_1 (.ButtonPress(L_F_Control_out), .Out(out_5));
  Button OperationControl (.out(OperationControl_out));
  ButtonController buttoncontroller_2 (.ButtonPress(OperationControl_out), .Out(out_4));
  Main main_1 (
    .A(A), .B(B), .Enable(Power), .Load_B(Load_out), .OP_code(out_4), .L___F(out_5),
    .Overflow(main_1_overflow), .Output(main_1_output), .MulCarryOut(main_1_mulcarryout));
  LED Overflow (.in(main_1_overflow));
  Hex_Digit_Display hex_digit_display_1 (.value(main_1_output));  // open: dp
  Hex_Digit_Display hex_digit_display_2 (.value(main_1_mulcarryout));  // open: dp

  // Notes on the sheet:
  //   00 - LOAD
  //   01 - FETCH A
  //   10 - FETCH B
  //   11 - OPERATIONS
  //   Result
  //   MulCarry
  //   00 - ADD
  //   01 - SUB
  //   10 - OR
  //   11 - MULTIPLY
  //   Result - Operation Output
  //   MulCarry - Carry from Multiplication Operation
endmodule

// BCNT
module ButtonController (
  input  ButtonPress,
  output [1:0] Out
);

  Counter #(.width(2), .max('h3)) counter_1 (.Q(Out), .clk(ButtonPress));  // open: load, D, count, carry, clr
endmodule
