// Logisim project mem_.circ as structural Verilog: 2 circuits, main circuit BC
module BC (
  input  in_1,
  input  in_2,
  input  in_3,
  input  in_4,
  output out_5
);

  wire and_1_out, and_2_out, not_1_out, not_2_out, s_r_ff_1_q;

  not not_1 (not_1_out, in_2);
  not not_2 (not_2_out, in_4);
  and and_1 (and_1_out, in_1, not_1_out, not_2_out);
  and and_2 (and_2_out, in_2, in_1, not_2_out);
  S_R_Flip_Flop s_r_ff_1 (.S(and_2_out), .clk(in_3), .R(and_1_out), .Q(s_r_ff_1_q));  // open: Qn, preset, reset, en
  and and_3 (out_5, s_r_ff_1_q, in_1, in_4);
endmodule

module four_cross_four_module (
  input  in_1,
  input  in_2,
  input  in_3,
  input  in_4,
  input  [1:0] in_5,
  input  in_6
);

  wire bc_1_out_5, bc_2_out_5, bc_3_out_5, bc_4_out_5, bc_5_out_5, bc_6_out_5, bc_7_out_5, bc_8_out_5,
       bc_9_out_5, bc_10_out_5, bc_11_out_5, bc_12_out_5, bc_13_out_5, bc_14_out_5, bc_15_out_5, bc_16_out_5,
       clock_1_out, decoder_1_out0, decoder_1_out1, decoder_1_out2, decoder_1_out3, or_1_out, or_2_out,
       or_3_out, or_4_out;

  Decoder #(.select(2), .enable("false")) decoder_1 (
    .out0(decoder_1_out0), .out1(decoder_1_out1), .out2(decoder_1_out2), .out3(decoder_1_out3), .sel(in_5));
  Clock clock_1 (.out(clock_1_out));
  BC bc_1 (.in_2(in_1), .in_3(clock_1_out), .in_1(decoder_1_out0), .in_4(in_6), .out_5(bc_1_out_5));
  BC bc_2 (.in_2(in_1), .in_3(clock_1_out), .in_1(decoder_1_out1), .in_4(in_6), .out_5(bc_2_out_5));
  BC bc_3 (.in_2(in_1), .in_3(clock_1_out), .in_1(decoder_1_out2), .in_4(in_6), .out_5(bc_3_out_5));
  BC bc_4 (.in_2(in_1), .in_3(clock_1_out), .in_1(decoder_1_out3), .in_4(in_6), .out_5(bc_4_out_5));
  or or_1 (or_1_out, bc_3_out_5, bc_2_out_5, bc_1_out_5, bc_4_out_5);
  LED led_1 (.in(or_1_out));
  BC bc_5 (.in_2(in_2), .in_3(clock_1_out), .in_1(decoder_1_out0), .in_4(in_6), .out_5(bc_5_out_5));
  BC bc_6 (.in_2(in_2), .in_3(clock_1_out), .in_1(decoder_1_out1), .in_4(in_6), .out_5(bc_6_out_5));
  BC bc_7 (.in_2(in_2), .in_3(clock_1_out), .in_1(decoder_1_out2), .in_4(in_6), .out_5(bc_7_out_5));
  BC bc_8 (.in_2(in_2), .in_3(clock_1_out), .in_1(decoder_1_out3), .in_4(in_6), .out_5(bc_8_out_5));
  or or_2 (or_2_out, bc_7_out_5, bc_6_out_5, bc_5_out_5, bc_8_out_5);
  LED led_2 (.in(or_2_out));
  BC bc_9 (.in_2(in_3), .in_3(clock_1_out), .in_1(decoder_1_out0), .in_4(in_6), .out_5(bc_9_out_5));
  BC bc_10 (.in_2(in_3), .in_3(clock_1_out), .in_1(decoder_1_out1), .in_4(in_6), .out_5(bc_10_out_5));
  BC bc_11 (.in_2(in_3), .in_3(clock_1_out), .in_1(decoder_1_out2), .in_4(in_6), .out_5(bc_11_out_5));
  BC bc_12 (.in_2(in_3), .in_3(clock_1_out), .in_1(decoder_1_out3), .in_4(in_6), .out_5(bc_12_out_5));
  BC bc_13 (.in_2(in_4), .in_3(clock_1_out), .in_1(decoder_1_out0), .in_4(in_6), .out_5(bc_13_out_5));
  BC bc_14 (.in_2(in_4), .in_3(clock_1_out), .in_1(decoder_1_out1), .in_4(in_6), .out_5(bc_14_out_5));
  BC bc_15 (.in_2(in_4), .in_3(clock_1_out), .in_1(decoder_1_out2), .in_4(in_6), .out_5(bc_15_out_5));
  BC bc_16 (.in_2(in_4), .in_3(clock_1_out), .in_1(decoder_1_out3), .in_4(in_6), .out_5(bc_16_out_5));
  or or_3 (or_3_out, bc_11_out_5, bc_10_out_5, bc_9_out_5, bc_12_out_5);
  LED led_3 (.in(or_3_out));
  or or_4 (or_4_out, bc_16_out_5, bc_15_out_5, bc_14_out_5, bc_13_out_5);
  LED led_4 (.in(or_4_out));
endmodule
